# Fritzing sketch flame_sensor (saved by Fritzing 0.9.3b)
breadboards: 1

parts:
  Part1 = Arduino Uno (Rev3)
  S1 = KY-026
  LED2 = smd LED [color="Red (633nm)" package="0805 [SMD]"]
  R1 = Resistor [tolerance=±5% resistance=220 package="2010 [SMD]"]

nets:
  N1: Part1.D8, S1.pin4
  N2: Part1.D13/SCK, R1.Pin_0
  N3: Part1.5V, S1.pin3
  N4: Part1.GND, S1.pin2, LED2.cathode
  N5: LED2.anode, R1.Pin_1

custom parts:
  KY-026: ky-026 flame sensor module
